# Fritzing sketch ArduPanTilt (saved by Fritzing 0.9.4)
circuit board: 10.4196cm x 5.77991cm

parts:
  Arduino_Uno = Arduino Uno (Rev3)
  Servo_PAN = Basic Servo
  LM_7805 = Voltage Regulator - 5V [package="TO220 [THT]"]
  Joystick = Thumb Joystick
  VCC = Battery block 9V
  Servo_TILT = Basic Servo

nets:
  N1: Arduino_Uno.A0, Joystick.HORZ
  N2: Arduino_Uno.A1, Joystick.VERT
  N3: Arduino_Uno.D9_PWM, Servo_TILT.pulse
  N4: Arduino_Uno.D10_PWM/SS, Servo_PAN.pulse
  GND: Arduino_Uno.GND, Servo_PAN.gnd, LM_7805.GND, Joystick.GND, VCC.-, Servo_TILT.gnd
  N5: Arduino_Uno.D7, Joystick.SEL
  5V: Arduino_Uno.5V, Joystick.VCC
  N6: Arduino_Uno.VIN, LM_7805.input_voltage, VCC.+
  VCC: Servo_PAN.vcc, LM_7805.output_voltage, Servo_TILT.vcc
